# Fritzing sketch extended wiring diagram (saved by Fritzing 0.9.3b)
breadboards: 2

parts:
  Arduino_Uno = Arduino Uno (Rev3)
  photodiod_1 = Photocell (LDR) [package=THT]
  laser_1 = LED - 5mm [color="Red (633nm)" package="5 mm [THT]"]
  start_button = Pushbutton [package="[THT]"]
  stop_button = Pushbutton [package="[THT]"]
  R1 = Resistor [tolerance=±5% resistance=10k package="0402 [SMD]"]
  R6 = Resistor [tolerance=±5% resistance=220 package="0402 [SMD]"]
  SP1 = SPEAKER [package=pcb_mount_speaker]
  U1 = LCD-16X2 [package=lcd-16x2_noholes]
  U2 = POT [package=pot_mammoth]
  Bauteil1 = LCD1602-I2C

nets (from the schematic view):
  N1: Arduino_Uno.A0, photodiod_1.pin_1, R1.Pin_1
  N2: Arduino_Uno.A4/SDA, Bauteil1.SDA
  N3: Arduino_Uno.A5/SCL, Bauteil1.SCL
  N4: Arduino_Uno.D8, U1.RS
  N5: Arduino_Uno.D9_PWM, U1.R_W
  N6: Arduino_Uno.D10_PWM/SS, U1.E
  N7: Arduino_Uno.D11_PWM/MOSI, U1.DB4
  N8: Arduino_Uno.D12/MISO, U1.DB6
  N9: Arduino_Uno.D2, start_button.Pin_1, start_button.Pin_2
  N10: Arduino_Uno.D3_PWM, stop_button.Pin_1, stop_button.Pin_2
  N11: Arduino_Uno.D5_PWM, SP1.-
  N12: Arduino_Uno.D7, U1.VO
  5V: Arduino_Uno.5V, laser_1.anode, R1.Pin_0, U1.VDD, U1.A, U2.E, Bauteil1.VCC
  GND: Arduino_Uno.GND, photodiod_1.pin_0, start_button.Pin_3, start_button.Pin_4, stop_button.Pin_3, stop_button.Pin_4, R6.Pin_1, SP1.+, U1.VSS, U1.DB5, U1.K, U2.A, Bauteil1.GND
  N13: laser_1.cathode, R6.Pin_0
  N14: U1.DB7, U2.S

custom parts:
  LCD1602-I2C: A standard character display, usually with 2x16 characters. Comes in many colors with LCM1602 IIC attached.
