# Fritzing sketch wiring diagram 3.0 (saved by Fritzing 0.9.3b)
breadboards: 1

parts:
  Arduino_Uno = Arduino Uno (Rev3)
  WeMos_D1_Mini2 = WeMos D1 Mini
  photodiod_1 = KY-018 Photoresistor Module [package="Breakout board"]
  Laser1 = LED - 5mm [color="Red (633nm)" package="5 mm [THT]"]
  VCC1 = Battery block 9V
  R1 = Resistor [tolerance=±5% resistance=470 package="0603 [SMD]"]
  photodiod_2 = KY-018 Photoresistor Module [package="Breakout board"]
  Laser2 = LED - 5mm [color="Red (633nm)" package="5 mm [THT]"]
  VCC2 = Battery block 9V
  R2 = Resistor [tolerance=±5% resistance=470 package="0603 [SMD]"]
  photodiod_3 = KY-018 Photoresistor Module [package="Breakout board"]
  Laser3 = LED - 5mm [color="Red (633nm)" package="5 mm [THT]"]
  VCC3 = Battery block 9V
  R3 = Resistor [tolerance=±5% resistance=470 package="0603 [SMD]"]
  SP1 = SPEAKER [package=pcb_mount_speaker]
  start_button = Round Pushbutton
  stop_button = Round Pushbutton

nets:
  N1: Arduino_Uno.A0, photodiod_1.S, photodiod_2.S, photodiod_3.S
  N2: Arduino_Uno.D9_PWM, SP1.-
  N3: Arduino_Uno.D11_PWM/MOSI, stop_button.leg0
  N4: Arduino_Uno.D12/MISO, start_button.leg0
  N5: Arduino_Uno.GND, WeMos_D1_Mini2.G, photodiod_1.-, photodiod_2.-, photodiod_3.-, SP1.+, start_button.leg1, stop_button.leg1
  N6: Arduino_Uno.D0/RX, WeMos_D1_Mini2.TX
  N7: Arduino_Uno.D1/TX, WeMos_D1_Mini2.RX
  VIN: Arduino_Uno.5V, WeMos_D1_Mini2.5V, photodiod_1.Vin, photodiod_2.Vin, photodiod_3.Vin
  N8: Laser1.cathode, VCC1.-
  N9: Laser1.anode, R1.Pin_0
  N10: VCC1.+, R1.Pin_1
  N11: Laser2.cathode, VCC2.-
  N12: Laser2.anode, R2.Pin_0
  N13: VCC2.+, R2.Pin_1
  N14: Laser3.cathode, VCC3.-
  N15: Laser3.anode, R3.Pin_0
  N16: VCC3.+, R3.Pin_1

custom parts:
  KY-018 Photoresistor Module: KY-018 Photoresistor module, used to measure light intensity. It can determine the presence or absence of light.
