# Fritzing sketch wiring diagram (saved by Fritzing 0.9.3b)

parts:
  Arduino_Uno = Arduino Uno (Rev3)
  photodiod_1 = KY-018 Photoresistor Module [package="Breakout board"]
  VCC1 = Battery block 9V
  R1 = Resistor [tolerance=±5% resistance=470 package="0603 [SMD]"]
  photodiod_2 = KY-018 Photoresistor Module [package="Breakout board"]
  VCC2 = Battery block 9V
  R2 = Resistor [tolerance=±5% resistance=470 package="0603 [SMD]"]
  photodiod_3 = KY-018 Photoresistor Module [package="Breakout board"]
  VCC3 = Battery block 9V
  R3 = Resistor [tolerance=±5% resistance=470 package="0603 [SMD]"]
  SP1 = SPEAKER [package=pcb_mount_speaker]
  start_button = Round Pushbutton
  stop_button = Round Pushbutton
  LED1 = LED - 5mm [color="Red (633nm)" package="5 mm [THT]"]
  R4 = Resistor [tolerance=±5% resistance=220 package=THT]
  LED2 = LED - 5mm [color="Red (633nm)" package="5 mm [THT]"]
  R5 = Resistor [tolerance=±5% resistance=220 package=THT]
  LED3 = LED - 5mm [color="Red (633nm)" package="5 mm [THT]"]
  R6 = Resistor [tolerance=±5% resistance=220 package=THT]
  D1 = Rectifier Diode [part_number=1N4001 package="300 mil [THT]"]
  D2 = Rectifier Diode [part_number=1N4001 package="300 mil [THT]"]
  D3 = Rectifier Diode [part_number=1N4001 package="300 mil [THT]"]
  Laser3 = Red Laser diode [package="5 mm [THT]"]
  Laser2 = Red Laser diode [package="5 mm [THT]"]
  Laser1 = Red Laser diode [package="5 mm [THT]"]

nets:
  N1: Arduino_Uno.A0, photodiod_1.S, photodiod_2.S, photodiod_3.S, LED1.anode, LED2.anode, LED3.anode
  N2: Arduino_Uno.D9_PWM, SP1.-
  N3: Arduino_Uno.D11_PWM/MOSI, stop_button.leg0
  N4: Arduino_Uno.D12/MISO, start_button.leg0
  N5: Arduino_Uno.GND, photodiod_1.-, photodiod_2.-, photodiod_3.-, SP1.+, start_button.leg1, stop_button.leg1, D1.cathode, D2.cathode, D3.cathode
  VIN: Arduino_Uno.5V, photodiod_1.Vin, photodiod_2.Vin, photodiod_3.Vin
  N6: VCC1.-, Laser1.-
  N7: VCC1.+, R1.Pin_1
  N8: R1.Pin_0, Laser1.+
  N9: VCC2.-, Laser2.-
  N10: VCC2.+, R2.Pin_1
  N11: R2.Pin_0, Laser2.+
  N12: VCC3.-, Laser3.-
  N13: VCC3.+, R3.Pin_1
  N14: R3.Pin_0, Laser3.+
  N15: LED1.cathode, R4.Pin_1
  N16: R4.Pin_0, D1.anode
  N17: LED2.cathode, R5.Pin_1
  N18: R5.Pin_0, D2.anode
  N19: LED3.cathode, R6.Pin_1
  N20: R6.Pin_0, D3.anode

custom parts:
  KY-018 Photoresistor Module: KY-018 Photoresistor module, used to measure light intensity. It can determine the presence or absence of light.
  Red Laser diode: A generic red Laser
